# Fritzing sketch astable-step3 (saved by Fritzing 0.8.5b)
breadboards: 1

parts:
  C1 = Electrolytic Capacitor [capacitance=1µF package="100 mil [THT, electrolytic]"]  # not connected
  C2 = Electrolytic Capacitor [capacitance=1µF package="100 mil [THT, electrolytic]"]
  LED2 = LED - 5mm [color="Green (555nm)" package="5 mm [THT]"]
  Q2 = NPN-Transistor [package="TO92 [THT]"]
  Q3 = NPN-Transistor [package="TO92 [THT]"]
  LED1 = LED - 5mm [color="Green (555nm)" package="5 mm [THT]"]

nets:
  N1: C2.-, Q2.B
  N2: C2.+, Q3.C, LED1.cathode
  N3: LED2.cathode, Q2.C
