# Fritzing sketch astable-step6 (saved by Fritzing 0.8.5b)
breadboards: 1

parts:
  C1 = Electrolytic Capacitor [capacitance=1µF package="100 mil [THT, electrolytic]"]
  C2 = Electrolytic Capacitor [capacitance=1µF package="100 mil [THT, electrolytic]"]
  R3 = Resistor [tolerance=±5% resistance=10k package=THT]
  R4 = Resistor [tolerance=±5% resistance=10k package=THT]
  LED2 = LED - 5mm [color="Green (555nm)" package="5 mm [THT]"]
  Q2 = NPN-Transistor [package="TO92 [THT]"]
  Q3 = NPN-Transistor [package="TO92 [THT]"]
  LED1 = LED - 5mm [color="Green (555nm)" package="5 mm [THT]"]

nets:
  N1: C1.-, R4.Pin_0, Q3.B
  N2: C1.+, LED2.cathode, Q2.C
  N3: C2.-, R3.Pin_0, Q2.B
  N4: C2.+, Q3.C, LED1.cathode
  N5: R3.Pin_1, R4.Pin_1
  N6: Q2.E, Q3.E
