# Fritzing sketch led-switch-step4 (saved by Fritzing 0.8.5b)
breadboards: 1

parts:
  R2 = Resistor [tolerance=±1% resistance=150 package=THT]
  LED2 = LED - 5mm [color="Green (555nm)" package="5 mm [THT]"]
  S2 = Pushbutton [package="[THT]"]

nets:
  N1: R2.Pin_0, S2.Pin_1, S2.Pin_2
  N2: R2.Pin_1, LED2.anode
  N3: S2.Pin_3, S2.Pin_4
