# Fritzing sketch mosfet-not-step1 (saved by Fritzing 0.8.5b)
breadboards: 1

parts:
  LED1 = LED - 5mm [color="Green (555nm)" package="5 mm [THT]"]  # not connected
  S1 = Pushbutton (square 0.2") [package="[THT]"]

nets:
  N1: S1.Pin_1, S1.Pin_2
  N2: S1.Pin_3, S1.Pin_4

custom parts:
  Pushbutton (square 0.2"): A generic 0.2" x 0.2" pushbutton.
