# Fritzing sketch mosfet_nand_step1 (saved by Fritzing 0.8.5b)
breadboards: 1

parts:
  S1 = Pushbutton (square 0.2") [package="[THT]"]
  R2 = Resistor [tolerance=±5% resistance=10k package=THT]
  R4 = Resistor [tolerance=±5% resistance=150 package=THT]
  LED2 = LED - 5mm [color="Green (555nm)" package="5 mm [THT]"]

nets:
  N1: S1.Pin_1, S1.Pin_2
  N2: S1.Pin_3, S1.Pin_4, R2.Pin_1, LED2.anode
  N3: R2.Pin_0, R4.Pin_0
  N4: R4.Pin_1, LED2.cathode

custom parts:
  Pushbutton (square 0.2"): A generic 0.2" x 0.2" pushbutton.
