# Fritzing sketch mosfet_nand_step4 (saved by Fritzing 0.8.5b)
breadboards: 1

parts:
  S1 = Pushbutton (square 0.2") [package="[THT]"]
  S2 = Pushbutton (square 0.2") [package="[THT]"]
  LED2 = LED - 5mm [color="Green (555nm)" package="5 mm [THT]"]
  LED3 = LED - 5mm [color="Green (555nm)" package="5 mm [THT]"]
  Q2 = PNP-Transistor [package="TO92 [THT]"]
  Q3 = PNP-Transistor [package="TO92 [THT]"]
  Q4 = NPN-Transistor [package="TO92 [THT]"]
  Q5 = NPN-Transistor [package="TO92 [THT]"]
  R2 = Resistor [tolerance=±1% resistance=10k package=THT]
  R4 = Resistor [tolerance=±1% resistance=150 package=THT]
  R5 = Resistor [tolerance=±1% resistance=10k package=THT]
  R6 = Resistor [tolerance=±1% resistance=150 package=THT]

nets:
  N1: S1.Pin_1, S1.Pin_2, S2.Pin_1, S2.Pin_2, Q2.E, Q3.E
  N2: S1.Pin_3, S1.Pin_4, LED2.anode, R2.Pin_1
  N3: S2.Pin_3, S2.Pin_4, LED3.anode, R5.Pin_1
  N4: LED2.cathode, R4.Pin_1
  N5: LED3.cathode, R6.Pin_1
  N6: Q3.C, Q4.E
  N7: Q4.C, Q5.E
  N8: Q5.C, R2.Pin_0, R4.Pin_0, R5.Pin_0, R6.Pin_0

custom parts:
  Pushbutton (square 0.2"): A generic 0.2" x 0.2" pushbutton.
