# Fritzing sketch mosfet_not_step1 (saved by Fritzing 0.8.5b)
breadboards: 1

parts:
  LED1 = LED - 5mm [color="Green (555nm)" package="5 mm [THT]"]
  S2 = Pushbutton (square 0.2") [package="[THT]"]

nets:
  N1: LED1.anode, S2.Pin_3, S2.Pin_4
  N2: S2.Pin_1, S2.Pin_2

custom parts:
  Pushbutton (square 0.2"): A generic 0.2" x 0.2" pushbutton.
