# Fritzing sketch mosfet_not_step3 (saved by Fritzing 0.8.5b)
breadboards: 1

parts:
  LED1 = LED - 5mm [color="Green (555nm)" package="5 mm [THT]"]
  Q1 = PNP-Transistor [package="TO92 [THT]"]  # not connected
  S1 = Pushbutton (square 0.2") [package="[THT]"]
  R1 = Resistor [tolerance=±1% resistance=10k package=THT]
  R2 = Resistor [tolerance=±1% resistance=150 package=THT]

nets:
  N1: LED1.cathode, R2.Pin_1
  N2: LED1.anode, S1.Pin_3, S1.Pin_4, R1.Pin_1
  N3: S1.Pin_1, S1.Pin_2
  N4: R1.Pin_0, R2.Pin_0

custom parts:
  Pushbutton (square 0.2"): A generic 0.2" x 0.2" pushbutton.
