# Fritzing sketch capacitors-series (saved by Fritzing 0.8.5b)
breadboards: 1

parts:
  S2 = Pushbutton (square 0.2") [package="[THT]"]
  C2 = Electrolytic Capacitor [capacitance=1µF package="100 mil [THT, electrolytic]"]
  LED2 = LED - 5mm [color="Green (555nm)" package="5 mm [THT]"]
  R1 = Resistor [tolerance=±1% resistance=150 package=THT]
  LED1 = LED - 5mm [color="Green (555nm)" package="5 mm [THT]"]
  C1 = Electrolytic Capacitor [capacitance=1µF package="100 mil [THT, electrolytic]"]
  S1 = Pushbutton (square 0.2") [package="[THT]"]
  R2 = Resistor [tolerance=±1% resistance=150 package=THT]

nets:
  GND: S2.Pin_1, S2.Pin_2, C1.-
  N1: S2.Pin_3, S2.Pin_4, LED2.cathode
  N2: C2.-, C1.+
  N3: C2.+, R1.Pin_0, R2.Pin_1
  N4: LED2.anode, R2.Pin_0
  N5: R1.Pin_1, LED1.cathode
  N6: LED1.anode, S1.Pin_1, S1.Pin_2
  5V: S1.Pin_3, S1.Pin_4

custom parts:
  Pushbutton (square 0.2"): A generic 0.2" x 0.2" pushbutton.
