# Fritzing sketch resistors-parallel (saved by Fritzing 0.8.5b)
breadboards: 1

parts:
  LED1 = LED - 5mm [color="Green (555nm)" package="5 mm [THT]"]
  S1 = Pushbutton (square 0.2") [package="[THT]"]
  R2 = Resistor [tolerance=±1% resistance=150 package=THT]
  R1 = Resistor [tolerance=±1% resistance=150 package=THT]

nets:
  GND: LED1.cathode
  N1: LED1.anode, R2.Pin_1, R1.Pin_1
  N2: S1.Pin_1, S1.Pin_2, R2.Pin_0
  5V: S1.Pin_3, S1.Pin_4, R1.Pin_0

custom parts:
  Pushbutton (square 0.2"): A generic 0.2" x 0.2" pushbutton.
