# Fritzing sketch simple-circuit (saved by Fritzing 0.8.7b)
breadboards: 1

parts:
  LED1 = LED - 5mm [color="Green (555nm)" package="5 mm [THT]"]
  R1 = Resistor [tolerance=±1% resistance=150 package=THT]

nets:
  GND: LED1.cathode
  N1: LED1.anode, R1.Pin_1
  5V: R1.Pin_0
