# Fritzing sketch bistable_final (saved by Fritzing 0.8.5b)
breadboards: 1

parts:
  Q8 = NPN-Transistor [package="TO92 [THT]"]
  Q9 = NPN-Transistor [package="TO92 [THT]"]
  R15 = Resistor [tolerance=±5% resistance=10k package=THT]
  R16 = Resistor [tolerance=±5% resistance=10k package=THT]
  R17 = Resistor [tolerance=±5% resistance=150 package=THT]
  R18 = Resistor [tolerance=±5% resistance=150 package=THT]
  LED7 = LED - 5mm [color="Green (555nm)" package="5 mm [THT]"]
  LED8 = LED - 5mm [color="Green (555nm)" package="5 mm [THT]"]

nets:
  N1: Q8.E, Q9.E
  N2: Q8.B, R16.Pin_1
  N3: Q8.C, R15.Pin_1, LED8.cathode
  N4: Q9.B, R15.Pin_0
  N5: Q9.C, R16.Pin_0, LED7.cathode
  N6: R17.Pin_0, LED7.anode
  N7: R17.Pin_1, R18.Pin_1
  N8: R18.Pin_0, LED8.anode
