# Fritzing sketch bistable_step2 (saved by Fritzing 0.8.5b)
breadboards: 1

parts:
  Q8 = NPN-Transistor [package="TO92 [THT]"]
  Q9 = NPN-Transistor [package="TO92 [THT]"]
  LED7 = LED - 5mm [color="Green (555nm)" package="5 mm [THT]"]
  LED8 = LED - 5mm [color="Green (555nm)" package="5 mm [THT]"]

nets:
  N1: Q8.C, LED8.cathode
  N2: Q9.C, LED7.cathode
