# Fritzing sketch bistable_step4 (saved by Fritzing 0.8.5b)
breadboards: 1

parts:
  Q8 = NPN-Transistor [package="TO92 [THT]"]
  Q9 = NPN-Transistor [package="TO92 [THT]"]
  R15 = Resistor [tolerance=±5% resistance=10k package=THT]
  R16 = Resistor [tolerance=±5% resistance=10k package=THT]
  LED7 = LED - 5mm [color="Green (555nm)" package="5 mm [THT]"]
  LED8 = LED - 5mm [color="Green (555nm)" package="5 mm [THT]"]

nets:
  N1: Q8.B, R16.Pin_1
  N2: Q8.C, R15.Pin_1, LED8.cathode
  N3: Q9.B, R15.Pin_0
  N4: Q9.C, R16.Pin_0, LED7.cathode
