# Fritzing sketch monostable_final (saved by Fritzing 0.8.5b)
breadboards: 1

parts:
  Q6 = NPN-Transistor [package="TO92 [THT]"]
  Q7 = NPN-Transistor [package="TO92 [THT]"]
  C5 = Electrolytic Capacitor [capacitance=1µF package="100 mil [THT, electrolytic]"]
  R16 = Resistor [tolerance=±5% resistance=10k package=THT]
  R17 = Resistor [tolerance=±5% resistance=10k package=THT]
  R18 = Resistor [tolerance=±5% resistance=150 package=THT]
  R19 = Resistor [tolerance=±5% resistance=150 package=THT]
  LED5 = LED - 5mm [color="Green (555nm)" package="5 mm [THT]"]
  LED6 = LED - 5mm [color="Green (555nm)" package="5 mm [THT]"]

nets:
  N1: Q6.E, Q7.E
  N2: Q6.B, R16.Pin_1
  N3: Q6.C, C5.+, LED6.cathode
  N4: Q7.B, C5.-, R17.Pin_0
  N5: Q7.C, R16.Pin_0, LED5.cathode
  N6: R17.Pin_1, R18.Pin_1, R19.Pin_1
  N7: R18.Pin_0, LED5.anode
  N8: R19.Pin_0, LED6.anode
