# Fritzing sketch multivibrators-all (saved by Fritzing 0.8.5b)
breadboards: 1

parts:
  C1 = Electrolytic Capacitor [capacitance=1µF package="100 mil [THT, electrolytic]"]
  C2 = Electrolytic Capacitor [capacitance=1µF package="100 mil [THT, electrolytic]"]
  R1 = Resistor [tolerance=±5% resistance=150 package=THT]
  R2 = Resistor [tolerance=±5% resistance=150 package=THT]
  R3 = Resistor [tolerance=±5% resistance=10k package=THT]
  R4 = Resistor [tolerance=±5% resistance=10k package=THT]
  LED1 = LED - 5mm [color="Green (555nm)" package="5 mm [THT]"]
  LED2 = LED - 5mm [color="Green (555nm)" package="5 mm [THT]"]
  Q2 = NPN-Transistor [package="TO92 [THT]"]
  Q3 = NPN-Transistor [package="TO92 [THT]"]
  Q4 = NPN-Transistor [package="TO92 [THT]"]
  Q5 = NPN-Transistor [package="TO92 [THT]"]
  C3 = Electrolytic Capacitor [capacitance=1µF package="100 mil [THT, electrolytic]"]
  R6 = Resistor [tolerance=±5% resistance=150 package=THT]
  R7 = Resistor [tolerance=±5% resistance=10k package=THT]
  R8 = Resistor [tolerance=±5% resistance=150 package=THT]
  LED3 = LED - 5mm [color="Green (555nm)" package="5 mm [THT]"]
  LED4 = LED - 5mm [color="Green (555nm)" package="5 mm [THT]"]
  R9 = Resistor [tolerance=±5% resistance=10k package=THT]
  Q6 = NPN-Transistor [package="TO92 [THT]"]
  Q7 = NPN-Transistor [package="TO92 [THT]"]
  R10 = Resistor [tolerance=±5% resistance=150 package=THT]
  R11 = Resistor [tolerance=±5% resistance=10k package=THT]
  R13 = Resistor [tolerance=±5% resistance=150 package=THT]
  LED5 = LED - 5mm [color="Green (555nm)" package="5 mm [THT]"]
  LED6 = LED - 5mm [color="Green (555nm)" package="5 mm [THT]"]
  R14 = Resistor [tolerance=±5% resistance=10k package=THT]

nets:
  N1: C1.-, LED1.cathode, Q3.C
  N2: C1.+, R4.Pin_0, Q2.B
  N3: C2.-, LED2.cathode, Q2.C
  N4: C2.+, R3.Pin_0, Q3.B
  N5: R1.Pin_0, LED1.anode
  N6: R1.Pin_1, R2.Pin_1, R3.Pin_1, R4.Pin_1, R6.Pin_1, R7.Pin_1, R8.Pin_1, R10.Pin_1, R13.Pin_1
  N7: R2.Pin_0, LED2.anode
  N8: Q2.E, Q3.E, Q4.E, Q5.E, Q6.E, Q7.E
  N9: Q4.B, R9.Pin_0
  N10: Q4.C, C3.-, LED3.cathode
  N11: Q5.B, C3.+, R7.Pin_0
  N12: Q5.C, LED4.cathode, R9.Pin_1
  N13: R6.Pin_0, LED4.anode
  N14: R8.Pin_0, LED3.anode
  N15: Q6.B, R11.Pin_0
  N16: Q6.C, LED5.cathode, R14.Pin_0
  N17: Q7.B, R14.Pin_1
  N18: Q7.C, R11.Pin_1, LED6.cathode
  N19: R10.Pin_0, LED5.anode
  N20: R13.Pin_0, LED6.anode
